// Logisim project alu.circ as structural Verilog: 1 circuit, main circuit main
module main (
  input  [15:0] X,
  input  [15:0] Y,
  input  [2:0] Switch,
  output Equal,
  output [15:0] Result,
  output [15:0] Result_2
);

  wire [15:0] add, \and , lt, mul, \or , sll, srl, \xor ;

  Shifter #(.width(16)) shifter_1 (.in(X), .\dist (Y[3:0]), .out(sll));
  Shifter #(.width(16), .shift("lr")) shifter_2 (.in(X), .\dist (Y[3:0]), .out(srl));
  Adder #(.width(16)) adder_1 (.a(X), .b(Y), .out(add));  // open: cin, cout
  assign \and  = X & Y;  // AND_Gate and_1, 16 bits wide
  assign \or  = X | Y;  // OR_Gate or_1, 16 bits wide
  assign \xor  = X ^ Y;  // XOR_Gate xor_1, 16 bits wide
  Comparator #(.width(16)) comparator_1 (.a(X), .b(Y), .eq(Equal), .lt(lt[0]));  // open: gt
  Multiplier #(.width(16)) multiplier_1 (.a(X), .b(Y), .out(mul), .cout(Result_2));  // open: cin
  Multiplexer #(.select(3), .width(16), .disabled(0), .enable("false")) multiplexer_1 (
    .in0(sll), .in1(srl), .in2(add), .in3(\and ), .in4(\or ), .in5(\xor ), .in6(lt), .in7(mul), .out(Result),
    .sel(Switch));

  // Other names for the same wires on the sheet: S[2:0] = Switch

  // Notes on the sheet:
  //   INPUTS to your circuit
  //   DON'T CHANGE THE LOCATIONS OF THE INPUTS AND OUTPUTS!
  //   OUTPUTS from your circuit
endmodule
