// Logisim project regfile.circ as structural Verilog: 1 circuit, main circuit main
module main (
  input  [2:0] Read_Register_1,
  input  [2:0] Read_Register_2,
  input  [2:0] Write_Register,
  input  [15:0] Write_Data,
  input  Write_Enable,
  input  Clock,
  output [15:0] s0_Value,
  output [15:0] s1_Value,
  output [15:0] s2_Value,
  output [15:0] ra_Value,
  output [15:0] sp_Value,
  output [15:0] Read_Data_1,
  output [15:0] Read_Data_2
);

  wire _01_w, _02_w, _03_w, _04_w, _05_w, _06_w, _07_w, write_enable_t;
  wire [15:0] _05_o, _06_o;

  Register #(.width(16)) register_1 (.D(Write_Data), .en(_01_w), .Q(ra_Value), .clk(Clock));  // open: clr
  Register #(.width(16)) register_2 (.D(Write_Data), .en(_02_w), .Q(s0_Value), .clk(Clock));  // open: clr
  Register #(.width(16)) register_3 (.D(Write_Data), .en(_03_w), .Q(s1_Value), .clk(Clock));  // open: clr
  Register #(.width(16)) register_4 (.D(Write_Data), .en(_04_w), .Q(s2_Value), .clk(Clock));  // open: clr
  Register #(.width(16)) register_5 (.D(Write_Data), .en(_05_w), .Q(_05_o), .clk(Clock));  // open: clr
  Register #(.width(16)) register_6 (.D(Write_Data), .en(_06_w), .Q(_06_o), .clk(Clock));  // open: clr
  Register #(.width(16)) register_7 (.D(Write_Data), .en(_07_w), .Q(sp_Value), .clk(Clock));  // open: clr
  Demultiplexer #(.select(3), .disabled(0)) demultiplexer_1 (
    .out1(_01_w), .out2(_02_w), .out3(_03_w), .out4(_04_w), .out5(_05_w), .out6(_06_w), .out7(_07_w),
    .in(Write_Enable), .sel(Write_Register), .en(write_enable_t));  // open: out0
  Multiplexer #(.select(3), .width(16), .disabled(0), .enable("false")) multiplexer_1 (
    .in0({16{1'b0}}), .in1(ra_Value), .in2(s0_Value), .in3(s1_Value), .in4(s2_Value), .in5(_05_o),
    .in6(_06_o), .in7(sp_Value), .out(Read_Data_1), .sel(Read_Register_1));
  Multiplexer #(.select(3), .width(16), .disabled(0), .enable("false")) multiplexer_2 (
    .in0({16{1'b0}}), .in1(ra_Value), .in2(s0_Value), .in3(s1_Value), .in4(s2_Value), .in5(_05_o),
    .in6(_06_o), .in7(sp_Value), .out(Read_Data_2), .sel(Read_Register_2));

  // Other names for the same wires on the sheet: _01_o[15:0] = ra_Value; _02_o[15:0] = s0_Value;
  //   _03_o[15:0] = s1_Value; _04_o[15:0] = s2_Value; _07_o[15:0] = sp_Value; clk = Clock;
  //   read_data1[15:0] = Read_Data_1; read_data2[15:0] = Read_Data_2; read_reg1[2:0] = Read_Register_1;
  //   read_reg2[2:0] = Read_Register_2; write_en = Write_Enable; write_reg[2:0] = Write_Register

  // Notes on the sheet:
  //   INPUTS to your circuit
  //   DON'T CHANGE THE LOCATIONS OF THE INPUTS AND OUTPUTS!
  //   These are DEBUG/TEST outputs from your circuit.
  //   OUTPUTS from your circuit
endmodule
